# Fritzing sketch Motores-DC (saved by Fritzing 0.9.0b)
breadboards: 1

parts:
  Parte1 = Arduino Uno (Rev3)
  VCC1 = Battery block 9V
  IC2 = L293D [package=THT]
  M1 = DC Motor
  M2 = DC Motor
  IR1 = TSOP312.., 314.. [package=THT]
  C1 = Ceramic Capacitor [capacitance="100 nF" package="0603 [SMD, multilayer]"]  # not connected
  C2 = Ceramic Capacitor [capacitance="100 nF" package="0603 [SMD, multilayer]"]  # not connected

nets:
  N1: Parte1.D8, IC2.In_2
  N2: Parte1.D9_PWM, IC2.In_1
  N3: Parte1.D10_PWM/SS, IC2.Enable_1
  N4: Parte1.D11_PWM/MOSI, IC2.Enable_2
  N5: Parte1.D12/MISO, IC2.In_4
  N6: Parte1.D13/SCK, IC2.In_3
  N7: Parte1.GND, VCC1.-, IC2.0V, IR1.Vs
  N8: Parte1.D2, IR1.GND
  N9: Parte1.5V, IC2.+V
  N10: Parte1.VIN, VCC1.+, IC2.+Vmotor, IR1.Data
  N11: IC2.Out_1_(_Controlled_by_Enable_1_), M2.pin_2
  N12: IC2.Out_2_(_Controlled_by_Enable_1_), M2.pin_1
  N13: IC2.Out_3_(_Controlled_by_Enable_2_), M1.pin_2
  N14: IC2.Out_4_(_Controlled_by_Enable_2_), M1.pin_1
