# Fritzing sketch Motores-DC (saved by Fritzing 0.9.0b)
breadboards: 1

parts:
  Parte1 = Arduino Uno (Rev3)
  IC2 = L293D [package=THT]
  M1 = DC Motor
  M2 = DC Motor
  IR1 = TSOP312.., 314.. [package=THT]
  C1 = Ceramic Capacitor [capacitance="100 nF" package="0603 [SMD, multilayer]"]  # not connected
  C2 = Ceramic Capacitor [capacitance="100 nF" package="0603 [SMD, multilayer]"]  # not connected
  VCC1 = Battery block 9V
  LED1 = LED - 5mm [color="Red (633nm)" package="5 mm [THT]"]
  R1 = Resistor [tolerance=±5% resistance=220 package=THT]
  S1 = Toggle Switch [package=THT]
  Parte2 = SRF05 Ultrasonic Rangefinder

nets:
  N1: Parte1.D8, IC2.In_2
  N2: Parte1.D9_PWM, IC2.In_1
  N3: Parte1.D12/MISO, IC2.In_4
  N4: Parte1.D13/SCK, IC2.In_3
  GND: Parte1.GND, IC2.0V, IR1.GND, VCC1.-, LED1.cathode, Parte2.GND
  N5: Parte1.D2, IR1.Data
  N6: Parte1.D4, R1.Pin_1
  N7: Parte1.D5_PWM, Parte2.Trig
  N8: Parte1.D6_PWM, Parte2.Echo
  N9: Parte1.5V, IC2.+V
  VIN: Parte1.VIN, IC2.+Vmotor, IR1.Vs, S1.COM, Parte2.VCC
  N10: IC2.Out_1_(_Controlled_by_Enable_1_), M2.pin_2
  N11: IC2.Out_2_(_Controlled_by_Enable_1_), M2.pin_1
  N12: IC2.Out_3_(_Controlled_by_Enable_2_), M1.pin_2
  N13: IC2.Out_4_(_Controlled_by_Enable_2_), M1.pin_1
  N14: VCC1.+, S1.L2
  N15: LED1.anode, R1.Pin_0
